// Logisim project 17000912.circ as structural Verilog: 8 circuits, main circuit S-R Latch
module S_R_Latch (
  input  S,
  input  R,
  output Q_prime,
  output Q
);

  nor nor_1 (Q_prime, S, Q);
  nor nor_2 (Q, Q_prime, R);
endmodule

module S_R_Filpflop (
  input  S,
  input  R,
  output Q_prime,
  output Q
);

  wire and_1_out, and_2_out, clock_1_out;

  Clock clock_1 (.out(clock_1_out));
  and and_1 (and_1_out, S, clock_1_out);
  and and_2 (and_2_out, clock_1_out, R);
  nor nor_1 (Q_prime, and_1_out, Q);
  nor nor_2 (Q, Q_prime, and_2_out);
endmodule

module J_K_Flipflop (
  input  S,
  input  R,
  output Q_prime,
  output Q
);

  wire and_1_out, and_2_out, clock_1_out;

  Clock clock_1 (.out(clock_1_out));
  and and_1 (and_1_out, Q_prime, S, clock_1_out);
  and and_2 (and_2_out, clock_1_out, R, Q);
  nor nor_1 (Q_prime, and_1_out, Q);
  nor nor_2 (Q, Q_prime, and_2_out);
endmodule

module J_K_Latch (
  input  J,
  input  R,
  output Q_prime,
  output Q
);

  wire and_1_out, and_2_out;

  and and_1 (and_1_out, Q_prime, J);
  and and_2 (and_2_out, R, Q);
  nor nor_1 (Q_prime, and_1_out, Q);
  nor nor_2 (Q, Q_prime, and_2_out);
endmodule

module Binary_Counter (
  input  in_1,
  output out_2,
  output out_3,
  output out_4,
  output out_5,
  output out_6
);

  wire and_1_out, and_2_out, and_3_out, clock_1_out;

  and and_1 (and_1_out, in_1, out_2);
  and and_2 (and_2_out, and_1_out, out_3);
  and and_3 (and_3_out, and_2_out, out_4);
  Clock clock_1 (.out(clock_1_out));
  J_K_Flip_Flop j_k_ff_1 (.J(in_1), .clk(clock_1_out), .K(in_1), .Q(out_2));  // open: Qn, preset, en, reset
  J_K_Flip_Flop j_k_ff_2 (.J(and_1_out), .clk(clock_1_out), .K(and_1_out), .Q(out_3));  // open: Qn, preset, en, reset
  J_K_Flip_Flop j_k_ff_3 (.J(and_2_out), .clk(clock_1_out), .K(and_2_out), .Q(out_4));  // open: Qn, preset, en, reset
  J_K_Flip_Flop j_k_ff_4 (.J(and_3_out), .clk(clock_1_out), .K(and_3_out), .Q(out_5));  // open: Qn, preset, en, reset
  and and_4 (out_6, out_5, and_3_out);
endmodule

module D_Latch (
  input  D_In,
  input  Read_0____Write_1,
  output D_Out
);

  wire and_1_out, and_2_out, nor_1_out, not_1_out;

  not not_1 (not_1_out, D_In);
  and and_1 (and_1_out, D_In, Read_0____Write_1);
  and and_2 (and_2_out, not_1_out, Read_0____Write_1);
  nor nor_1 (nor_1_out, and_1_out, D_Out);
  nor nor_2 (D_Out, nor_1_out, and_2_out);
endmodule

module D_Filpflop (
  input  D_In,
  input  Read_0____Write_1,
  output D_Out
);

  wire and_1_out, and_2_out, clock_1_out, nor_1_out, not_1_out;

  Clock clock_1 (.out(clock_1_out));
  not not_1 (not_1_out, D_In);
  and and_1 (and_1_out, D_In, clock_1_out, Read_0____Write_1);
  and and_2 (and_2_out, not_1_out, clock_1_out, Read_0____Write_1);
  nor nor_1 (nor_1_out, and_1_out, D_Out);
  nor nor_2 (D_Out, nor_1_out, and_2_out);
endmodule

module _4bit_Register (
  input  in_1,
  input  in_2,
  input  in_3,
  input  in_4,
  output out_5,
  output out_6,
  output out_7,
  output out_8
);

  wire clock_1_out;

  Clock clock_1 (.out(clock_1_out));
  D_Flip_Flop d_ff_1 (.clk(clock_1_out), .D(in_1), .Q(out_5));  // open: Qn, preset, en, reset
  D_Flip_Flop d_ff_2 (.clk(clock_1_out), .D(in_2), .Q(out_6));  // open: Qn, preset, en, reset
  D_Flip_Flop d_ff_3 (.clk(clock_1_out), .D(in_3), .Q(out_7));  // open: Qn, preset, en, reset
  D_Flip_Flop d_ff_4 (.clk(clock_1_out), .D(in_4), .Q(out_8));  // open: Qn, preset, en, reset
endmodule
